// Logisim project 6651071061_LAB1_Bai7trang7.circ as structural Verilog: 1 circuit, main circuit main
module main (
  input  [3:0] Datain,
  input  [2:0] Addr,
  input  Load,
  output [3:0] Dataout
);

  wire clock_1_out, not_1_out;

  Clock clock_1 (.out(clock_1_out));
  not not_1 (not_1_out, Load);
  RAM #(.addrWidth(3), .dataWidth(4)) ram_1 (
    .addr(Addr), .data(Dataout), .sel(1'b1), .clk(clock_1_out), .ld(not_1_out));  // open: clr
  assign Dataout = Load ? Datain : 4'bz;  // Controlled_Buffer controlled_buffer_1

  // Notes on the sheet:
  //   Lê Đình Sơn - 6651071061
endmodule
